# Fritzing sketch Colpitts 2023-12-06 (saved by Fritzing 1.0.0rc)
circuit board: 6cm x 4.6cm
breadboards: 1

parts:
  R2 = Resistor [tolerance=±5% power=0.25W resistance=100k package=THT]
  R3 = Resistor [tolerance=±5% power=0.25W resistance=47k package=THT]
  L1 = Inductor [package="400 mil [THT]"]
  R4 = Resistor [tolerance=±5% power=0.25W resistance=2k package=THT]
  R1 = Resistor [tolerance=±5% power=0.25W resistance=100k package=THT]
  SMA = SMA Antenna Connector [package=sma-edge]
  GND = male pin header, 2 pins [form="♂ (male)"]
  C7 = Ceramic Capacitor [capacitance=1µF voltage=35V package="200 mil [THT, multilayer]"]
  C2 = Ceramic Capacitor [capacitance=680pF voltage=35V package="200 mil [THT, multilayer]"]
  C3 = Ceramic Capacitor [capacitance=220pF voltage=35V package="200 mil [THT, multilayer]"]
  C6 = Ceramic Capacitor [capacitance=1µF voltage=35V package="200 mil [THT, multilayer]"]
  C1 = Ceramic Capacitor [capacitance=3.3nF voltage=35V package="200 mil [THT, multilayer]"]
  +9V = Screw terminal - 2 pins [mn="+         -" package=THT]
  C4 = Ceramic Capacitor [capacitance=0F voltage=35V package="200 mil [THT, multilayer]"]
  SMA2 = SMA Antenna Connector [package=sma-edge]
  Q1 = NPN-Transistor [package="TO92 [THT]"]
  C5 = Ceramic Capacitor [capacitance=0F voltage=35V package="200 mil [THT, multilayer]"]

nets:
  N1: R2.Pin_0, R1.Pin_1
  N2: R2.Pin_1, R3.Pin_0, C7.1, Q1.B
  GND: R3.Pin_1, R4.Pin_1, SMA.GND, GND.pin2, C7.0, +9V.pin2, SMA2.GND
  N3: L1.pin_0, R1.Pin_0, C1.1, +9V.pin1
  N4: L1.pin_1, C2.0, C3.0, C6.1, C4.1, Q1.C, C5.1
  N5: R4.Pin_0, C2.1, C3.1, C1.0, C4.0, Q1.E, C5.0
  N6: SMA.SIGNAL, GND.pin1, C6.0, SMA2.SIGNAL

notes:
  Colpitts
  by DM9GP ver 2023.12.06
  +
  -
  SGN
